// Logisim project exerc1.circ as structural Verilog: 1 circuit, main circuit main
module main (
  input  in_1,
  input  in_2,
  input  in_3,
  input  in_4,
  input  in_5,
  input  in_6
);

  wire and_1_out, nand_1_out, nor_1_out;

  nor nor_1 (nor_1_out, in_1, in_2, in_3);
  nand nand_1 (nand_1_out, in_5, in_6);
  and and_1 (and_1_out, nor_1_out, in_4, nand_1_out);
  LED led_1 (.in(and_1_out));

  // Notes on the sheet:
  //   S1=!(A+B+C)
  //   S2=!(E*F)
  //   S=(S1*S2)*D
  //   S3=(!(A+B+C) + !(E*F)*D)
endmodule
